# Fritzing sketch Valve_Stepper_Control (saved by Fritzing 0.8.3b)
breadboards: 1

parts:
  Part1 = Arduino Uno (Rev3)
  S1 = Toggle Switch [package=THT]
  LED1 = LED - 5mm [color="Red (633nm)" package="5 mm [THT]"]
  M1 = Stepper Motor - Bipolar  # not connected
  MD09B1 = A4988 Stepper Motor Driver Carrier  # not connected
  U1 = LIPO-1000mAh [package=lipo-1000]  # not connected

nets:
  N1: Part1.GND, S1.L1, LED1.cathode
  N2: Part1.D13/SCK, S1.COM
  N3: Part1.D5_PWM, LED1.anode
  N4: Part1.5V, S1.L2

notes:
  Battery shown does not have enough voltage. Needs 8-35V.

custom parts:
  A4988 Stepper Motor Driver Carrier: The Pololu stepper motor driver carrier for the A4988 motor driver integrated circuits. http://www.pololu.com/catalog/product/1182 Utilized Király László initial part: http://fritzing.org/projects/dual-stepper-motor/
