# Fritzing sketch Initial igniter test Sketch (saved by Fritzing 0.8.3b)
breadboards: 1

parts:
  Composants1 = Arduino Uno (Rev3)
  S1 = Pushbutton [package="[SMD]"]
  LED1 = LED - 5mm [color="Red (633nm)" package="5 mm [THT]"]
  Q1 = MOSFET-NCHANNEL [package=to220v]
  R1 = Resistor [tolerance=±5% resistance=220 package=THT]
  R2 = Resistor [tolerance=±5% resistance=220 package=THT]
  LED2 = LED - 5mm [color="Red (633nm)" package="5 mm [THT]"]
  D1 = Rectifier Diode [part_number=1N4001 package="300 mil [THT]"]  # not connected
  Spark_Gap_Igniter = FUSE [package=fuse_5mm]
  Power_supply = Transformer [package=transformer]

nets:
  N1: Composants1.D8, Q1.G
  N2: Composants1.D12/MISO, S1.Pin_1, S1.Pin_2, R1.Pin_0
  N3: Composants1.5V, S1.Pin_3, S1.Pin_4
  N4: Composants1.GND, LED1.anode, Q1.S, Power_supply.3
  N5: LED1.cathode, R1.Pin_1
  N6: Q1.D, R2.Pin_0, Spark_Gap_Igniter.1
  N7: R2.Pin_1, LED2.cathode
  N8: LED2.anode, Power_supply.2
