# Fritzing sketch Stepper Test (saved by Fritzing 0.8.3b)
breadboards: 1

parts:
  Part1 = Arduino Uno (Rev3)
  S1 = Toggle Switch [package=THT]
  R1 = Resistor [tolerance=±5% resistance=220 package=THT]
  LED1 = LED - 5mm [color="Red (633nm)" package="5 mm [THT]"]
  M1 = Stepper Motor - Bipolar  # not connected
  U1 = LIPO-1000mAh [package=lipo-1000]  # not connected

nets:
  N1: Part1.GND, S1.L2, LED1.anode
  N2: Part1.D13/SCK, S1.COM
  N3: Part1.D5_PWM, R1.Pin_0
  N4: R1.Pin_1, LED1.cathode

notes:
  pins 6 and 7 are for the A4983 stepper driver they drive direction and step respectively
  Battery does not have enough volts
